# Fritzing sketch new main circuit (saved by Fritzing 0.9.3b)
stripboards: 1
perfboards: 1

parts:
  J1 = female pin header, 12 pins [form="♀ (female)"]  # not connected
  J2 = female pin header, 12 pins [form="♀ (female)"]  # not connected
  J3 = female pin header, 12 pins [form="♀ (female)"]  # not connected
  J4 = female pin header, 12 pins [form="♀ (female)"]  # not connected
  J5 = female pin header, 12 pins [form="♀ (female)"]  # not connected
  J6 = female pin header, 12 pins [form="♀ (female)"]  # not connected
  J7 = female pin header, 12 pins [form="♀ (female)"]  # not connected
  J8 = female pin header, 24 pins [form="♀ (female)"]
  J9 = female pin header, 24 pins [form="♀ (female)"]
  Teensy1 = Teensy 3.6 (Basic)
  IC1 = IC, DIP package, 16 pins [chip_label=4051]
  IC2 = IC, DIP package, 16 pins [chip_label=4051]
  IC3 = IC, DIP package, 16 pins [chip_label=4051]
  IC4 = IC, DIP package, 16 pins [chip_label=4051]
  R1 = Resistor [tolerance=±5% resistance=10k package=THT]
  J10 = female pin header, 12 pins [form="♀ (female)"]

nets:
  N1: J8.pin1, Teensy1.D33
  N2: J8.pin2, Teensy1.D34
  N3: J8.pin3, Teensy1.D35
  N4: J8.pin4, Teensy1.D36
  N5: J8.pin5, Teensy1.D37
  N6: J8.pin6, Teensy1.D38
  N7: J8.pin7, Teensy1.D39
  N8: J8.pin8, Teensy1.A21/DAC0
  N9: J8.pin9, Teensy1.A22/DAC1
  GND: J8.pin10, J9.pin24, Teensy1.GND, Teensy1.GND1, IC1.pin6, IC1.pin7, IC1.pin8, IC2.pin6, IC2.pin7, IC2.pin8, IC3.pin3, R1.Pin_0
  N10: J8.pin11, Teensy1.D13
  N11: J8.pin12, Teensy1.A0/D14
  N12: J8.pin13, Teensy1.A1/D15
  N13: J8.pin14, Teensy1.A2/D16
  N14: J8.pin15, Teensy1.A3/D17
  N15: J8.pin16, Teensy1.A4/D18
  N16: J8.pin17, Teensy1.A5/D19
  N17: J8.pin18, Teensy1.A6/D20
  N18: J8.pin19, Teensy1.A7/D21
  N19: J8.pin20, Teensy1.A8/D22
  N20: J8.pin21, Teensy1.A9/D23
  N21: J8.pin22, J9.pin10, Teensy1.3V3, Teensy1.3V3_1
  N22: J8.pin23, Teensy1.AGND
  N23: J8.pin24, Teensy1.Vin
  N24: J9.pin1, Teensy1.D32, IC3.pin9, IC4.pin9
  N25: J9.pin2, Teensy1.D31, IC3.pin10, IC4.pin10
  N26: J9.pin3, Teensy1.D30, IC3.pin11, IC4.pin11
  N27: J9.pin4, Teensy1.D29
  N28: J9.pin5, Teensy1.D28
  N29: J9.pin6, Teensy1.D27
  N30: J9.pin7, Teensy1.D26, IC4.pin3
  N31: J9.pin8, Teensy1.D25, IC2.pin3, R1.Pin_1
  N32: J9.pin9, Teensy1.D24, IC1.pin3
  N33: J9.pin11, Teensy1.D12
  N34: J9.pin12, Teensy1.D11
  N35: J9.pin13, Teensy1.D10
  N36: J9.pin14, Teensy1.D9
  N37: J9.pin15, Teensy1.D8
  N38: J9.pin16, Teensy1.D7
  N39: J9.pin17, Teensy1.D6
  N40: J9.pin18, Teensy1.D5
  N41: J9.pin19, Teensy1.D4, IC1.pin9, IC2.pin9
  N42: J9.pin20, Teensy1.D3, IC1.pin10, IC2.pin10
  N43: J9.pin21, Teensy1.D2, IC1.pin11, IC2.pin11
  N44: J9.pin22, Teensy1.D1
  N45: J9.pin23, Teensy1.D0
  N46: IC1.pin4, IC2.pin4, IC3.pin4
  N47: IC1.pin16, IC2.pin16, IC3.pin5, IC3.pin16, IC4.pin16
  N48: IC3.pin6, IC3.pin7, IC3.pin8, IC4.pin6, IC4.pin7, IC4.pin8
  N49: IC4.pin1, J10.pin12
  N50: J10.pin8, J10.pin9
  N51: J10.pin10, J10.pin11

custom parts:
  Teensy 3.6 (Basic): The Teensy is a complete USB-based microcontoller development system, in a very small footprint, capable of implementing many types of projects. All programming is done via the USB port. No special programmer is needed, only a standard micro-USB cable and a PC or Macintosh with a USB port.
